# Fritzing sketch autoding (saved by Fritzing 0.9.3b)
circuit board: 5.97568cm x 3.48716cm
stripboards: 1

parts:
  R4 = Resistor [tolerance=±5% resistance=1k package="0805 [SMD]"]
  C10 = Ceramic Capacitor [capacitance=22pF package="0805 [SMD, multilayer]"]
  C11 = Ceramic Capacitor [capacitance=22pF package="0805 [SMD, multilayer]"]
  U6 = atmega168 [package=dip]
  XTAL3 = Crystal [frequency="16 Mhz" package=SMD]
  JP1 = Header 4 [package=jst-4-pth]
  Q1 = NPN-Transistor [package="TO92 [THT]"]
  Q2 = NPN-Transistor [package="TO92 [THT]"]
  Q3 = NPN-Transistor [package="TO92 [THT]"]
  Q4 = NPN-Transistor [package="TO92 [THT]"]
  Q5 = NPN-Transistor [package="TO92 [THT]"]
  Q6 = NPN-Transistor [package="TO92 [THT]"]
  Q7 = NPN-Transistor [package="TO92 [THT]"]
  Q8 = NPN-Transistor [package="TO92 [THT]"]
  LED1 = LED - 3mm [color="Red (633nm)" package="3 mm [THT]"]

nets:
  N1: R4.Pin_0, U6.RESET, JP1.1
  N2: R4.Pin_1, U6.VCC, U6.AVCC, U6.AREF
  GND: C10.0, C11.1, U6.GND, JP1.4, Q1.E, Q2.E, Q3.E, Q4.E, Q5.E, Q6.E, Q7.E, Q8.E, LED1.cathode
  N3: C10.1, U6.XLAT1, XTAL3.pin_0
  N4: C11.0, U6.XLAT2, XTAL3.pin_1
  N5: U6.D0_(RX), JP1.3
  N6: U6.D1_(TX), JP1.2
  N7: U6.D10_(PWM), Q1.B
  N8: U6.D11_(PWM), Q2.B
  N9: U6.D12, Q3.B
  N10: U6.D13, Q4.B
  N11: U6.A0, Q5.B
  N12: U6.A1, Q6.B
  N13: U6.A2, Q7.B
  N14: U6.A3, Q8.B
  N15: U6.A4, LED1.anode
